# Fritzing sketch timer_attiny (saved by Fritzing 0.9.2b)
breadboards: 3

parts:
  U1 = 74HC595 [package="DIP16 [THT]"]
  U2 = ATTINY13 [package=dip]
  VCC1 = 4 x AAA Battery Mount
  U7 = 74HC595 [package="DIP16 [THT]"]
  U8 = 7-SEGMENT-DISPLAY [package=7-segment-display]
  U9 = 7-SEGMENT-DISPLAY [package=7-segment-display]
  R37 = Resistor [tolerance=±5% resistance=220 package=THT]
  R38 = Resistor [tolerance=±5% resistance=220 package=THT]
  R39 = Resistor [tolerance=±5% resistance=220 package=THT]
  R40 = Resistor [tolerance=±5% resistance=220 package=THT]
  R41 = Resistor [tolerance=±5% resistance=220 package=THT]
  R42 = Resistor [tolerance=±5% resistance=220 package=THT]
  R43 = Resistor [tolerance=±5% resistance=220 package=THT]
  R44 = Resistor [tolerance=±5% resistance=220 package=THT]
  R45 = Resistor [tolerance=±5% resistance=220 package=THT]
  R46 = Resistor [tolerance=±5% resistance=220 package=THT]
  R47 = Resistor [tolerance=±5% resistance=220 package=THT]
  R48 = Resistor [tolerance=±5% resistance=220 package=THT]
  R49 = Resistor [tolerance=±5% resistance=220 package=THT]
  R50 = Resistor [tolerance=±5% resistance=220 package=THT]
  R51 = Resistor [tolerance=±5% resistance=220 package=THT]
  R52 = Resistor [tolerance=±5% resistance=220 package=THT]

nets:
  N1: U1.Q1, R38.Pin_1
  N2: U1.Q2, R39.Pin_1
  N3: U1.Q3, R40.Pin_1
  N4: U1.Q4, R41.Pin_1
  N5: U1.Q5, R42.Pin_1
  N6: U1.Q6, R43.Pin_1
  N7: U1.Q7, R44.Pin_1
  GND: U1.GND, U1.OE, U2.GND, VCC1.-, U7.GND, U7.OE, U8.G1, U8.G2, U9.G1
  N8: U1.Q7', U7.DS
  VCC: U1.MR, U1.VCC, U2.VCC, VCC1.+, U7.MR, U7.VCC
  N9: U1.SH_CP, U2.PB1(MISO), U7.SH_CP
  N10: U1.ST_CP, U2.PB0(MOSI), U7.ST_CP
  N11: U1.DS, U2.PB2(SCK_ADC1)
  N12: U1.Q0, R37.Pin_1
  N13: U7.Q1, R46.Pin_1
  N14: U7.Q2, R47.Pin_1
  N15: U7.Q3, R49.Pin_1
  N16: U7.Q4, R48.Pin_1
  N17: U7.Q5, R52.Pin_1
  N18: U7.Q6, R51.Pin_1
  N19: U7.Q7, R45.Pin_1
  N20: U7.Q0, R50.Pin_1
  N21: U8.E, R37.Pin_0
  N22: U8.D, R41.Pin_0
  N23: U8.C, R42.Pin_0
  N24: U8.DP, R43.Pin_0
  N25: U8.B, R44.Pin_0
  N26: U8.A, R40.Pin_0
  N27: U8.F, R39.Pin_0
  N28: U8.G, R38.Pin_0

notes:
  /**
  * Shift Register Example
  * for 74HC595 456shift register
  * http://arduino.cc/en/Tutorial/ShiftOut
  * This sketch turns 8 LEDs on and of based on bytes
  * send to a 74HC595 shift register.
  *
  * based on Tim Igoes Sketch one by one
  * http://arduino.cc/en/Tutorial/ShftOut12
  *
  * Hardware:
  * * 74HC595 shift register attached to pins 8, 11, and 12 of the Arduino
  * * LEDs attached to each of the outputs of the shift register
  *
  * by Fabian Moron Zirfas
  *
  */
  //Pin connected to latch pin (ST_CP) of 74HC595
  const int latchPin = 0;
  //Pin connected to clock pin (SH_CP) of 74HC595
  const int clockPin = 1;
  //Pin connected to Data in (DS) of 74HC595
  const int dataPin = 2;
  //this holds our pattern an array of arrays (matrix)
  char vals [8][8] = {
  {'0','1','2','3','4','5','6','0'},
  {'4','2','2','3','5','7','0','3'},
  {'0','5','4','0','2','2','3','6'},
  {'2','7','2','6','6','4','1','4'},
  {'7','4','5','5','6','3','0','3'},
  {'3','3','5','7','7','1','4','3'},
  {'6','2','7','1','0','6','4','2'},
  {'5','1','3','0','0','5','7','6'}
  };
  void setup() {
  //set pins to output because they are addressed in the main loop
  pinMode(latchPin, OUTPUT);
  pinMode(dataPin, OUTPUT);
  pinMode(clockPin, OUTPUT);
  }
  void loop() {
  for(int i = 0; i < 8;i++){
  for(int j=0; j< 8; j++){
  registerWrite(vals[i][j], HIGH);
  delay(100); // wait a moment
  }
  }
  }
  // This method sends bits to the shift register:
  void registerWrite(char pin, int whichState) {
  // ASCII '0' through '9' characters are
  // represented by the values 48 through 57.
  // so if the you send a number from 0 through 7 in ASCII,
  // you can subtract 48 to get the actual value:
  int bitToSet = pin - 48;
  // the bits you want to send
  byte bitsToSend = 0;
  // turn off the output so the pins don't light up
  // while you're shifting bits:
  digitalWrite(latchPin, LOW);
  // turn on the next highest bit in bitsToSend:
  bitWrite(bitsToSend, bitToSet, whichState);
  // shift the bits out:
  shiftOut(dataPin, clockPin, MSBFIRST, bitsToSend);
  // turn on the output so the LEDs can light up:
  digitalWrite(latchPin, HIGH);
  }
